# Fritzing sketch Automated Lamp (saved by Fritzing 0.9.4)
breadboards: 1

parts:
  U1 = RELAY-SOLIDSTATE [package=relay-s108t02]
  LED1 = smd LED [color="Red (633nm)" package="0603 [SMD]"]
  LED2 = smd LED [color="Red (633nm)" package="0603 [SMD]"]
  Y1 = CRYSTAL [package=hc49u-v]
  U2 = atmega328 [package=dip]
  Power_RGB1 = Prolight RGB 3 Watt Star
  R1 = Resistor [tolerance=±5% resistance=220 package=THT]
  R2 = Resistor [tolerance=±5% resistance=220 package=THT]
  BAT1 = Battery Holders [package=battery-aa]
  BATT1 = FKIT-COIN_CELL [package=fkit-lir2450-h]

nets:
  N1: U1.T1, Power_RGB1.B+, Power_RGB1.G+, Power_RGB1.R+
  N2: U1.T2, BATT1.POS
  N3: U1.+, U2.D7
  N4: U1.-, LED1.cathode, LED2.cathode, U2.GND, BAT1.-
  N5: LED1.anode, R1.Pin_0
  N6: LED2.anode, R2.Pin_0
  N7: Y1.1, U2.XLAT2
  N8: Y1.2, U2.XLAT1
  N9: U2.VCC, U2.AVCC, U2.AREF, BAT1.+
  N10: U2.D5_(PWM), R1.Pin_1
  N11: U2.D6_(PWM), R2.Pin_1
  N12: Power_RGB1.R-, Power_RGB1.G-, Power_RGB1.B-, BATT1.NEG
